# Fritzing sketch ESP-01_RF_Transceiver (saved by Fritzing 0.9.4)
breadboards: 1

parts:
  U3 = ESP8266 WiFi Module [part_number=ESP8266]
  Bauteil1 = Adafruit Micro USB Breakout [part_number="Adafruit #1833"]
  433_MHz_Transmitter = FS1000A - 433Mhz RF Transmitter [package=THT]
  433_MHz_Receiver = XD-RF-5V [package=THT]
  U7 = Voltage Regulator - 3.3V [package="TO220 [THT]"]
  R1 = Resistor [tolerance=±5% resistance=10k package=THT]
  R2 = Resistor [tolerance=±5% resistance=10k package=THT]

nets:
  N1: U3.RXD, 433_MHz_Receiver.DATA#1
  VCC: U3.VCC, U3.GPIO_16, U3.CH_PD, 433_MHz_Transmitter.VCC, U7.output_voltage, R2.Pin_1
  N2: U3.GPIO_0, R1.Pin_0
  N3: U3.GPIO_2, R2.Pin_0
  GND: U3.GND, Bauteil1.GND, 433_MHz_Transmitter.GND, 433_MHz_Receiver.GND, U7.GND
  N4: Bauteil1.VBUS, U7.input_voltage

custom parts:
  ESP8266 WiFi Module: Generic WiFi Module based on the ESP8266 with onboard PCB antenna and UART communications
  Adafruit Micro USB Breakout: Simple but effective - this breakout board has a USB Micro-B connector, with all 5 pins broken out. Great for pairing with a microcontroller with USB support, or adding USB 5V power to a project. We use a micro-AB connector with through-hole shielding pads for an excellent strong connection - it won't rip off by accident! Comes with one fully assembled and tested micro B breakout PCB and a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
  FS1000A - 433Mhz RF Transmitter: This is 433Mhz RF transmitter with receiver kit for Arduino ARM MCU wireless Application environment: Remote control switch, receiver module, motorcycles, automobile anti-theft products, home security products, electric doors, shutter doors, windows, remote control socket, remote control LED, remote audio remote control electric doors, garage door remote control, remote control retractable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
  XD-RF-5V: This is 433Mhz RF transmitter with receiver kit for Arduino ARM MCU wireless Application environment: Remote control switch, receiver module, motorcycles, automobile anti-theft products, home security products, electric doors, shutter doors, windows, remote control socket, remote control LED, remote audio remote control electric doors, garage door remote control, remote control retractable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
